# Fritzing sketch envlogger_arduino_mega (saved by Fritzing 0.9.0b)
breadboards: 1

parts:
  Part1 = Arduino Mega 2560 (Rev3)
  DHT11 = Humidity and Temperature Sensor RHT03
  ESP8266_ESP-01_WiFi_Module = ESP8266 ESP01 [part_number=ESP8266 package=THT]

nets:
  N1: Part1.D15/RX3, ESP8266_ESP-01_WiFi_Module.TXD
  N2: Part1.D14/TX3, ESP8266_ESP-01_WiFi_Module.RXD
  3V3: Part1.3V3, ESP8266_ESP-01_WiFi_Module.VCC, ESP8266_ESP-01_WiFi_Module.CH_PD
  5V: Part1.5V, DHT11.Vcc
  GND: Part1.GND, DHT11.GND_2, ESP8266_ESP-01_WiFi_Module.GND
  N3: Part1.D2_PWM, DHT11.Data-signal

custom parts:
  ESP8266 ESP01: Generic WiFi Module based on the ESP8266 with onboard PCB antenna and UART communications
